# Fritzing sketch sketch (saved by Fritzing 0.8.7b)
breadboards: 1

parts:
  Part1 = Arduino Uno (Rev3) - ICSP
  J1 = Piezo Speaker
  RHT1 = Humidity and Temperature Sensor RHT03
  R1 = Resistor [tolerance=±5% resistance=10k package=THT]
  Part2 = SRF05 Ultrasonic Rangefinder
  Part3 = Bluetooth HC-05 Macho
  R3 = Resistor [tolerance=±5% resistance=1k package=THT]
  R4 = Resistor [tolerance=±5% resistance=1k package=THT]
  R5 = PHOTOCELL [package=photocell-kit]
  R6 = Resistor [tolerance=±5% resistance=560 package=THT]
  S1 = H-Bridge with L298N
  M1 = DC Motor
  M2 = DC Motor
  M3 = DC Motor  # not connected
  M4 = DC Motor  # not connected
  Stromversorgung_Beradboard1 = Stromversorgung Beradboard [package=THT]
  PSU1 = Adjustable Breadboard Power Supply

nets:
  N1: Part1.A0, R5.P$1, R6.Pin_0
  VCC: Part1.5V, RHT1.Vcc, R1.Pin_0, Part2.VCC, Part3.VCC, R5.P$2, Stromversorgung_Beradboard1.+5_/_+3_Volt_4#12, Stromversorgung_Beradboard1.Ground_1#15
  GND: Part1.GND, J1.pin1, RHT1.GND_2, Part2.GND, Part3.GND, R4.Pin_1, R6.Pin_1, Stromversorgung_Beradboard1.+5_/_+3_Volt_4#13, Stromversorgung_Beradboard1.Ground_1#14, PSU1.Vin2+
  N2: Part1.D8, Part3.TXD
  N3: Part1.D9_PWM, J1.pin2
  N4: Part1.D3_PWM, RHT1.Data-signal, R1.Pin_1
  N5: Part1.D5_PWM, Part2.Trig
  N6: Part1.D6_PWM, Part2.Echo
  N7: Part1.D7, R3.Pin_0
  N8: Part3.RXD, R3.Pin_1, R4.Pin_0
  N9: S1.OUT4-Motor2, M1.pin_1, M2.pin_1
  N10: Stromversorgung_Beradboard1.+5_Volt_1, Stromversorgung_Beradboard1.Ground_1#3
  N11: Stromversorgung_Beradboard1.+5_Volt_2, Stromversorgung_Beradboard1.Ground_2
  N12: Stromversorgung_Beradboard1.+5_Volt_3, Stromversorgung_Beradboard1.Ground_3
  N13: Stromversorgung_Beradboard1.+3_Volt_1, Stromversorgung_Beradboard1.Ground_4
  N14: Stromversorgung_Beradboard1.+3_Volt_2, Stromversorgung_Beradboard1.Ground_5
  N15: Stromversorgung_Beradboard1.+3_Volt_3, Stromversorgung_Beradboard1.Ground_6

custom parts:
  H-Bridge with L298N: h-bridge
